// Logisim project 20_apr_2016.circ as structural Verilog: 7 circuits, main circuit igual
module igual (
  input  a1,
  input  a0,
  input  b1,
  input  b0,
  output igual
);

  wire not_1_out, not_2_out, xor_1_out, xor_2_out;

  ExactlyOne xor_1 (.out(xor_1_out), .in1(a1), .in3(b1), .in4(b1));
  xor xor_2 (xor_2_out, a0, b0);
  not not_1 (not_1_out, xor_1_out);
  not not_2 (not_2_out, xor_2_out);
  and and_1 (igual, not_1_out, not_2_out);

  // Notes on the sheet:
  //   a = b
endmodule

module menor (
  input  a1,
  input  a0,
  input  b1,
  input  b0,
  output menor
);

  wire and_1_out, and_2_out, and_3_out, not_1_out, not_2_out;

  not not_1 (not_1_out, a1);
  not not_2 (not_2_out, a0);
  and and_1 (and_1_out, not_1_out, b1);
  and and_2 (and_2_out, not_1_out, not_2_out, b0);
  and and_3 (and_3_out, not_2_out, b1, b0);
  or or_1 (menor, and_1_out, and_2_out, and_3_out);

  // Notes on the sheet:
  //   a < b =1
endmodule

module maior (
  input  a1,
  input  a0,
  input  b1,
  input  b0,
  output maior
);

  wire and_1_out, and_2_out, and_3_out, not_1_out, not_2_out;

  not not_1 (not_1_out, b1);
  not not_2 (not_2_out, b0);
  and and_1 (and_1_out, a1, not_1_out);
  and and_2 (and_2_out, a1, a0, not_2_out);
  and and_3 (and_3_out, a0, not_1_out, not_2_out);
  or or_1 (maior, and_1_out, and_2_out, and_3_out);

  // Notes on the sheet:
  //   a > b = 1
endmodule

module comp2n2bcada (
  input  a1,
  input  a0,
  input  b1,
  input  b0,
  output igual,
  output menor,
  output maior
);

  igual igual_1 (.a1(a1), .a0(a0), .b1(b1), .b0(b0), .igual(igual));
  menor menor_1 (.a1(a1), .a0(a0), .b1(b1), .b0(b0), .menor(menor));
  maior maior_1 (.a1(a1), .a0(a0), .b1(b1), .b0(b0), .maior(maior));

  // Notes on the sheet:
  //   a1a0 vs b1b0
endmodule

module CompDasComp (
  input  igual1,
  input  menor1,
  input  maior1,
  input  igual0,
  input  menor0,
  input  maior0,
  output igual,
  output menor,
  output maior
);

  wire and_2_out, and_3_out;

  and and_1 (igual, igual1, igual0);
  and and_2 (and_2_out, igual1, menor0);
  and and_3 (and_3_out, igual1, maior0);
  or or_1 (menor, menor1, and_2_out);
  or or_2 (maior, maior1, and_3_out);
endmodule

module comp2n4bcada (
  input  a3,
  input  a2,
  input  a1,
  input  a0,
  input  b3,
  input  b2,
  input  b1,
  input  b0,
  output igual,
  output menor,
  output maior
);

  wire comp2n2bcada_1_igual, comp2n2bcada_1_maior, comp2n2bcada_1_menor, comp2n2bcada_2_igual,
       comp2n2bcada_2_maior, comp2n2bcada_2_menor;

  comp2n2bcada comp2n2bcada_1 (
    .a1(a3), .a0(a2), .b1(b3), .b0(b2), .igual(comp2n2bcada_1_igual), .menor(comp2n2bcada_1_menor),
    .maior(comp2n2bcada_1_maior));
  comp2n2bcada comp2n2bcada_2 (
    .a1(a1), .a0(a0), .b1(b1), .b0(b0), .igual(comp2n2bcada_2_igual), .menor(comp2n2bcada_2_menor),
    .maior(comp2n2bcada_2_maior));
  CompDasComp compdascomp_1 (
    .igual1(comp2n2bcada_1_igual), .menor1(comp2n2bcada_1_menor), .maior1(comp2n2bcada_1_maior),
    .igual0(comp2n2bcada_2_igual), .menor0(comp2n2bcada_2_menor), .maior0(comp2n2bcada_2_maior),
    .igual(igual), .menor(menor), .maior(maior));

  // Notes on the sheet:
  //   a3a2a1a0  vs  b3b2b1b0
endmodule

module comp2n8bcada (
  input  a7,
  input  a6,
  input  a5,
  input  a4,
  input  a3,
  input  a2,
  input  a1,
  input  a0,
  input  b7,
  input  b6,
  input  b5,
  input  b4,
  input  b3,
  input  b2,
  input  b1,
  input  b0,
  output igual,
  output menor,
  output maior
);

  wire comp2n4bcada_1_igual, comp2n4bcada_1_maior, comp2n4bcada_1_menor, comp2n4bcada_2_igual,
       comp2n4bcada_2_maior, comp2n4bcada_2_menor;

  comp2n4bcada comp2n4bcada_1 (
    .a3(a7), .a2(a6), .a1(a5), .a0(a4), .b3(b7), .b2(b6), .b1(b5), .b0(b4), .igual(comp2n4bcada_1_igual),
    .menor(comp2n4bcada_1_menor), .maior(comp2n4bcada_1_maior));
  comp2n4bcada comp2n4bcada_2 (
    .a3(a3), .a2(a2), .a1(a1), .a0(a0), .b3(b3), .b2(b2), .b1(b1), .b0(b0), .igual(comp2n4bcada_2_igual),
    .menor(comp2n4bcada_2_menor), .maior(comp2n4bcada_2_maior));
  CompDasComp compdascomp_1 (
    .igual1(comp2n4bcada_1_igual), .menor1(comp2n4bcada_1_menor), .maior1(comp2n4bcada_1_maior),
    .igual0(comp2n4bcada_2_igual), .menor0(comp2n4bcada_2_menor), .maior0(comp2n4bcada_2_maior),
    .igual(igual), .menor(menor), .maior(maior));

  // Notes on the sheet:
  //   a7a6a5a4a3a2a1a0   vs    b7b6b5b4b3b2b1b0
endmodule
