// Logisim project Helena_R_S_DEspindula-06-05-2016.circ as structural Verilog: 3 circuits, main circuit ULA
module ULA (
  input  [15:0] menos_sig,
  input  [2:0] in_2,
  input  [15:0] menos_sig_2
);

  wire and_1_out, and_2_out, and_3_out, and_4_out, bit_extender_1_out, decoder_1_out0, decoder_1_out1,
       decoder_1_out2, decoder_1_out3, neg, or_1_out, overf1, overf2, overf3;
  wire [3:0] multiplexer_1_out, multiplexer_1_out_2;
  wire [15:0] aritimetica_1_out_3, aritimetica_1_out_5, aritimetica_1_out_7, aritimetica_1_out_9, igual,
       logica_1_out_3, logica_1_out_5, logica_1_out_6;
  wire [15:8] multiplexer_1_out_3;

  Decoder #(.select(3)) decoder_1 (
    .out0(decoder_1_out0), .out1(decoder_1_out1), .out2(decoder_1_out2), .out3(decoder_1_out3), .sel(in_2));  // open: out4, out5, out6, out7, en
  and and_1 (and_1_out, overf1, decoder_1_out0);
  and and_2 (and_2_out, overf2, decoder_1_out2);
  and and_3 (and_3_out, overf3, decoder_1_out3);
  or or_1 (or_1_out, and_1_out, and_2_out, and_3_out);
  aritimetica aritimetica_1 (
    .in_1(menos_sig), .in_2(menos_sig_2), .out_3(aritimetica_1_out_3), .Overflow__1(overf1),
    .out_5(aritimetica_1_out_5), .Negativo(neg), .out_7(aritimetica_1_out_7), .Overflow__2(overf2),
    .out_9(aritimetica_1_out_9), .Overflow__3(overf3));
  logica logica_1 (
    .in_1(menos_sig), .in_2(menos_sig_2), .out_3(logica_1_out_3), .out_4(igual), .out_5(logica_1_out_5),
    .out_6(logica_1_out_6));
  and and_4 (and_4_out, decoder_1_out1, neg);
  Multiplexer #(.select(3), .width(16)) multiplexer_1 (
    .in0(aritimetica_1_out_3), .in1(aritimetica_1_out_5), .in2(aritimetica_1_out_7),
    .in3(aritimetica_1_out_9), .in4(logica_1_out_3), .in5(igual), .in6(logica_1_out_5), .in7(logica_1_out_6),
    .out({multiplexer_1_out_3, multiplexer_1_out_2, multiplexer_1_out}), .sel(in_2));  // open: en
  Bit_Extender #(.in_width(16), .out_width(1)) bit_extender_1 (.in(igual), .out(bit_extender_1_out));
  Hex_Digit_Display hex_digit_display_1 (.value(multiplexer_1_out_3[15:12]));  // open: dp
  Hex_Digit_Display hex_digit_display_2 (.value(multiplexer_1_out_3[11:8]));  // open: dp
  Hex_Digit_Display hex_digit_display_3 (.value(multiplexer_1_out_2));  // open: dp
  LED led_1 (.in(bit_extender_1_out));
  LED led_2 (.in(or_1_out));
  LED led_3 (.in(and_4_out));
  Hex_Digit_Display hex_digit_display_4 (.value(multiplexer_1_out));  // open: dp

  // Other names for the same wires on the sheet: operacao[2:0] = in_2

  // Notes on the sheet:
  //   000 -> A + B
  //   001 -> A - B
  //   010 -> A*2
  //   011 -> B*2
  //   100 -> A > B
  //   101 -> A = B
  //   110 -> A < B
  //   111 -> A or B
  //   Legenda Operações
  //   Número B
  //   Número A
  //   A comparação da igualdade é feita independente da operação escolhida
  //   Overflow só ativa a flag se a sua respectiva soma for a operação escolhida (000, 010 e 011)
  //   Negativo só ativa a flag se a operação escolhida for subtração (001)
  //   Display Hexadecimal
  //   Flags
  //   Iguais
  //   Overflow
  //   Negativo
endmodule

module aritimetica (
  input  [15:0] in_1,
  input  [15:0] in_2,
  output [15:0] out_3,
  output Overflow__1,
  output [15:0] out_5,
  output Negativo,
  output [15:0] out_7,
  output Overflow__2,
  output [15:0] out_9,
  output Overflow__3
);

  Adder #(.width(16)) adder_1 (.a(in_1), .b(in_2), .out(out_3), .cin(1'b0), .cout(Overflow__1));
  Subtractor #(.width(16)) subtractor_1 (.a(in_1), .b(in_2), .out(out_5), .bin(1'b0), .bout(Negativo));
  Adder #(.width(16)) adder_2 (.a(in_1), .b(in_1), .out(out_7), .cin(1'b0), .cout(Overflow__2));
  Adder #(.width(16)) adder_3 (.a(in_2), .b(in_2), .out(out_9), .cin(1'b0), .cout(Overflow__3));

  // Notes on the sheet:
  //   Número A
  //   Número B
  //   Soma de A com B
  //   Subtração de A e B
  //   Soma de A e A (ou A*2)
  //   Soma de B e B (ou B*2)
endmodule

module logica (
  input  [15:0] in_1,
  input  [15:0] in_2,
  output [15:0] out_3,
  output [15:0] out_4,
  output [15:0] out_5,
  output [15:0] out_6
);

  wire comparator_1_eq, comparator_1_gt, comparator_1_lt;

  Comparator #(.width(16)) comparator_1 (
    .a(in_1), .b(in_2), .gt(comparator_1_gt), .eq(comparator_1_eq), .lt(comparator_1_lt));
  assign out_6 = in_1 ^ in_2;  // XOR_Gate xor_1, 16 bits wide
  assign out_3 = {{15{1'b0}}, comparator_1_gt};  // Bit_Extender bit_extender_1
  assign out_4 = {{15{1'b0}}, comparator_1_eq};  // Bit_Extender bit_extender_2
  assign out_5 = {{15{1'b0}}, comparator_1_lt};  // Bit_Extender bit_extender_3

  // Notes on the sheet:
  //   Número A
  //   Número B
  //   A > B
  //   A = B
  //   A < B
  //   A ou B
endmodule
